# Fritzing sketch Circuit (saved by Fritzing 0.9.3b)
breadboards: 1

parts:
  IC1 = IC, DIP package, 12 pins [chip_label=IC]
  BAT3 = Battery Holders [package=battcom_20mm_pth]
  R2 = Basic Flex Resistor
  R3 = Basic Flex Resistor
  R4 = Resistor [tolerance=±5% resistance=10k package=THT]
  R1 = Resistor [tolerance=±5% resistance=10k package=THT]

nets:
  N1: IC1.pin1, BAT3.+, R2.pin_1, R3.pin_1
  N2: IC1.pin6, BAT3.-, R3.Pin_2, R4.Pin_1, R1.Pin_1
  N3: IC1.pin9, R1.Pin_0
  N4: IC1.pin10, R2.Pin_2, R4.Pin_0
